# Fritzing sketch Nodo_compass_ (saved by Fritzing 0.9.3b)

parts:
  Componente1 = Triple Axis Magnetometer - HMC5883 Breakout
  Componente4 = Arduino Uno (Rev3) - ICSP

nets:
  GND: Componente1.GND, Componente4.GND
  VCC: Componente1.VCC, Componente4.5V
  N1: Componente1.SDA, Componente4.D5_PWM
  N2: Componente1.SCL, Componente4.D6_PWM

notes:
  Compass
  RX pin 6
  TX pin 5
  COMPASS NODE ARDUINO UNO
