# Fritzing sketch Nodo_compass_lidar_servo (saved by Fritzing 0.9.3b)
breadboards: 1

parts:
  Componente1 = Triple Axis Magnetometer - HMC5883 Breakout
  J1 = Basic Servo
  Componente3 = LIDAR-Lite
  Componente4 = Arduino Uno (Rev3) - ICSP

nets:
  GND: Componente1.GND, J1.gnd, Componente3.GND, Componente4.GND
  VCC: Componente1.VCC, J1.vcc, Componente3.5V, Componente4.5V
  N1: Componente1.SDA, Componente4.D5_PWM
  N2: Componente1.SCL, Componente4.D6_PWM
  N3: J1.pulse, Componente4.D2
  N4: Componente3.SCL, Componente4.D4
  N5: Componente3.SDA, Componente4.D3_PWM

notes:
  Compass
  RX pin 6
  TX pin 5
  Lidar
  RX pin 3
  TX pin 4
  LIDAR COMPASS NODE ARDUINO UNO

custom parts:
  LIDAR-Lite: PulsedLight LIDAR-Lite Sensor
