# Fritzing sketch Sonar_Switch_Node_Arduino_Nano (saved by Fritzing 0.9.3b)
breadboards: 1

parts:
  Componente1 = Arduino Nano (Rev3.0)
  hc-sr1 = hc-sr04
  hc-sr2 = hc-sr04
  hc-sr3 = hc-sr04
  D2F1 = D2F-FL Omron Snap Action Limit Switch with Level
  D2F2 = D2F-FL Omron Snap Action Limit Switch with Level
  D2F3 = D2F-FL Omron Snap Action Limit Switch with Level

nets:
  N1: Componente1.D2, hc-sr3.Echo
  N2: Componente1.D3, hc-sr3.Trig
  N3: Componente1.D4, hc-sr2.Echo
  N4: Componente1.D5, hc-sr2.Trig
  N5: Componente1.D6, hc-sr1.Echo
  N6: Componente1.D7, hc-sr1.Trig
  N7: Componente1.D8, D2F3.NO
  N8: Componente1.D9, D2F2.NO
  N9: Componente1.D10, D2F1.NO
  GND: Componente1.GND, hc-sr1.GND, hc-sr2.GND, hc-sr3.GND
  VCC: Componente1.5V, hc-sr1.VCC, hc-sr2.VCC, hc-sr3.VCC, D2F1.COM, D2F2.COM, D2F3.COM

notes:
  Front Sonar
  Echo 2
  Trig 3
  Right Sonar
  Echo 4
  Trig 5
  Left Sonar
  Echo 6
  Trig 7

custom parts:
  D2F-FL Omron Snap Action Limit Switch with Level: Snap action switch with stainless steel lever.
