# Fritzing sketch Motor_Microswitch_Node (saved by Fritzing 0.9.3b)
breadboards: 1

parts:
  S1 = H-Bridge with L298N
  Componente1 = Arduino Nano (Rev3.0)
  S2 = H-Bridge with L298N
  M1 = DC Motor
  M2 = DC Motor
  M3 = DC Motor
  M4 = DC Motor
  BAT1 = Battery Holders [package=lipo-1100mAh]
  BAT2 = Battery Holders [package=lipo-1100mAh]
  D2F1 = D2F-FL Omron Snap Action Limit Switch with Level
  D2F2 = D2F-FL Omron Snap Action Limit Switch with Level
  D2F3 = D2F-FL Omron Snap Action Limit Switch with Level
  R2 = Resistor [tolerance=±5% resistance=10k package="0402 [SMD]"]
  R3 = Resistor [tolerance=±5% resistance=10k package="0402 [SMD]"]
  BAT3 = Battery Holders [package=lipo-1100mAh]
  R1 = Resistor [tolerance=±5% resistance=10k package="0402 [SMD]"]

nets:
  N1: S1.ENA, S1.ENB, Componente1.D3
  N2: S1.IN1, S1.IN3, Componente1.D2
  N3: S1.IN2, S1.IN4, Componente1.D4
  N4: S1.M1-01, M3.pin_2
  N5: S1.M1-02, M3.pin_1
  N6: S1.M2-01, M4.pin_2
  N7: S1.M2-02, M4.pin_1
  N8: S1.ENA-5V, Componente1.5V, S2.ENA-5V, D2F1.COM, D2F3.COM, R1.Pin_0
  N9: Componente1.D5, S2.IN1, S2.IN3
  N10: Componente1.D6, S2.ENA, S2.ENB
  N11: Componente1.D7, S2.IN2, S2.IN4
  N12: Componente1.D8, D2F1.NO, R3.Pin_1
  N13: Componente1.D9, D2F2.NO, R2.Pin_1
  N14: Componente1.D10, D2F3.NO, R1.Pin_1
  N15: Componente1.GND, D2F2.COM, R2.Pin_0, R3.Pin_0
  N16: S2.M1-01, M1.pin_2
  N17: S2.M1-02, M1.pin_1
  N18: S2.M2-01, M2.pin_2
  N19: S2.M2-02, M2.pin_1
  N20: BAT1.+, BAT2.+, BAT3.+
  N21: BAT2.-, BAT3.-

notes:
  I pin IN1 e IN3 vanno collegati in parallelo al PIN2
  I pin IN2 e IN4 vanno collegati in Parallelo al PIN4
  I pin ENA e ENB vanno collegati in Parallelo al PIN3
  I pin IN1 e IN3 vanno collegati in parallelo al PIN4
  I pin IN2 e IN4 vanno collegati in Parallelo al PIN6
  I pin ENA e ENB vanno collegati in Parallelo al PIN5
  Microswitch NC, 10k ohm.
  PIN8. PIN9. PIN10

custom parts:
  H-Bridge with L298N: h-bridge
  D2F-FL Omron Snap Action Limit Switch with Level: Snap action switch with stainless steel lever.
